// Logisim project alu.circ as structural Verilog: 1 circuit, main circuit alu
module alu (
  input  [31:0] A,
  input  [31:0] B,
  input  [3:0] ALUSel,
  output [31:0] Result
);

  wire comparator_1_lt;
  wire [31:0] add0, and1, divu8, mul10, mulh14, mulhu11, or2, remu9, sll6, slt7, sra5, srl4, sub12, xor3;

  Adder #(.width(32)) adder_1 (.a(A), .b(B), .out(add0));  // open: cin, cout
  assign and1 = A & B;  // AND_Gate and_1, 32 bits wide
  assign or2 = A | B;  // OR_Gate or_1, 32 bits wide
  assign xor3 = A ^ B;  // XOR_Gate xor_1, 32 bits wide
  Shifter #(.shift("lr"), .width(32)) shifter_1 (.in(A), .\dist (B[4:0]), .out(srl4));
  Shifter #(.shift("ar"), .width(32)) shifter_2 (.in(A), .\dist (B[4:0]), .out(sra5));
  Shifter #(.width(32)) shifter_3 (.in(A), .\dist (B[4:0]), .out(sll6));
  Comparator #(.width(32)) comparator_1 (.a(A), .b(B), .lt(comparator_1_lt));  // open: gt, eq
  Divider #(.width(32)) divider_1 (.a(A), .b(B), .out(divu8));  // open: upper, rem
  Divider #(.width(32)) divider_2 (.a(A), .b(B), .rem(remu9));  // open: out, upper
  Multiplier #(.mode("twosComplement"), .width(32)) multiplier_1 (.a(A), .b(B), .out(mul10));  // open: cin, cout
  Multiplier #(.width(32)) multiplier_2 (.a(A), .b(B), .cout(mulhu11));  // open: out, cin
  Subtractor #(.width(32)) subtractor_1 (.a(A), .b(B), .out(sub12));  // open: bin, bout
  Multiplier #(.mode("twosComplement"), .width(32)) multiplier_3 (.a(A), .b(B), .cout(mulh14));  // open: out, cin
  assign slt7 = {{31{1'b0}}, comparator_1_lt};  // Bit_Extender bit_extender_1
  Multiplexer #(.enable("false"), .select(4), .width(32)) multiplexer_1 (
    .in0(add0), .in1(and1), .in2(or2), .in3(xor3), .in4(srl4), .in5(sra5), .in6(sll6), .in7(slt7),
    .in8(divu8), .in9(remu9), .in10(mul10), .in11(mulhu11), .in12(sub12), .in13(B), .in14(mulh14),
    .out(Result), .sel(ALUSel));  // open: in15

  // Other names for the same wires on the sheet: bsel13[31:0] = B

  // Notes on the sheet:
  //   INPUTS to your circuit
  //   DON'T CHANGE THE LOCATIONS OF THE INPUTS AND OUTPUTS!
  //   OUTPUT from your circuit
endmodule
