// Logisim project control_logic.circ as structural Verilog: 1 circuit, main circuit control_logic
module control_logic (
  input  [31:0] inst,
  input  BrEq,
  input  BrLt,
  output PCSel,
  output RegWEn,
  output [2:0] ImmSel,
  output BrUn,
  output ASel,
  output BSel,
  output [3:0] ALUSel,
  output MemRW,
  output [1:0] WBSel,
  output CSRSel,
  output CSRWen
);

  wire add_alu, and_1_out, and_2_out, and_3_out, and_4_out, and_5_out, and_6_out, and_7_out, and_8_out,
       and_21_out, and_22_out, and_24_out, and_25_out, and_26_out, and_alu, bsel_alu, comparator_1_eq,
       comparator_2_eq, comparator_3_eq, comparator_4_eq, comparator_5_eq, comparator_6_eq, comparator_7_eq,
       comparator_8_eq, comparator_9_eq, comparator_10_eq, comparator_11_eq, comparator_12_eq,
       comparator_13_eq, comparator_14_eq, comparator_15_eq, comparator_16_eq, comparator_17_eq,
       comparator_18_eq, comparator_19_eq, comparator_20_eq, comparator_21_eq, comparator_22_eq,
       comparator_23_eq, comparator_24_eq, comparator_25_eq, comparator_26_eq, comparator_27_eq,
       comparator_28_eq, comparator_29_eq, comparator_30_eq, comparator_32_eq, comparator_33_eq,
       comparator_34_eq, comparator_35_eq, comparator_36_eq, comparator_37_eq, comparator_38_eq,
       comparator_39_eq, comparator_40_eq, comparator_41_eq, comparator_42_eq, comparator_45_eq,
       comparator_46_eq, comparator_48_eq, comparator_49_eq, comparator_50_eq, comparator_51_eq,
       comparator_54_eq, comparator_55_eq, I_Type, mul_alu, mulh_alu, mulhu_alu, nor_4_out, not_1_out,
       not_2_out, not_3_out, not_4_out, not_5_out, or_1_out, or_2_out, or_3_out, or_4_out, or_5_out,
       or_6_out, or_7_out, or_8_out, or_10_out, or_11_out, or_12_out, or_13_out, or_14_out, or_15_out,
       or_21_out, or_22_out, or_23_out, or_24_out, or_25_out, or_alu, R_Type, S_Type, SB_Type, sll_alu,
       slt_alu, sra_alu, srl_alu, sub_alu, U_Type, UJ_Type, WBSel_mem, xor_alu;

  Comparator #(.width(3)) comparator_1 (.a(3'b000), .b(inst[14:12]), .eq(comparator_1_eq));  // open: gt, lt
  not not_1 (not_1_out, BrEq);
  Comparator #(.width(3)) comparator_2 (.a(3'b001), .b(inst[14:12]), .eq(comparator_2_eq));  // open: gt, lt
  Comparator #(.width(3)) comparator_3 (.a(3'b100), .b(inst[14:12]), .eq(comparator_3_eq));  // open: gt, lt
  not not_2 (not_2_out, BrLt);
  Comparator #(.width(3)) comparator_4 (.a(3'b101), .b(inst[14:12]), .eq(comparator_4_eq));  // open: gt, lt
  Comparator #(.width(3)) comparator_5 (.a(3'b110), .b(inst[14:12]), .eq(comparator_5_eq));  // open: gt, lt
  not not_3 (not_3_out, BrLt);
  Comparator #(.width(3)) comparator_6 (.a(3'b111), .b(inst[14:12]), .eq(comparator_6_eq));  // open: gt, lt
  Comparator #(.width(7)) comparator_7 (.a(7'b0010011), .b(inst[6:0]), .eq(comparator_7_eq));  // open: gt, lt
  Comparator #(.width(3)) comparator_8 (.a(3'b000), .b(inst[14:12]), .eq(comparator_8_eq));  // open: gt, lt
  Comparator #(.width(7)) comparator_9 (.a(7'b0000001), .b(inst[31:25]), .eq(comparator_9_eq));  // open: gt, lt
  Comparator #(.width(7)) comparator_10 (.a(7'b0000001), .b(inst[31:25]), .eq(comparator_10_eq));  // open: gt, lt
  Comparator #(.width(3)) comparator_11 (.a(3'b001), .b(inst[14:12]), .eq(comparator_11_eq));  // open: gt, lt
  Comparator #(.width(7)) comparator_12 (.a(7'b0000001), .b(inst[31:25]), .eq(comparator_12_eq));  // open: gt, lt
  Comparator #(.width(7)) comparator_13 (.a(7'b0100000), .b(inst[31:25]), .eq(comparator_13_eq));  // open: gt, lt
  and and_1 (and_1_out, BrEq, comparator_1_eq);
  and and_2 (and_2_out, not_1_out, comparator_2_eq);
  and and_3 (and_3_out, BrLt, comparator_3_eq);
  and and_4 (and_4_out, not_2_out, comparator_4_eq);
  and and_5 (and_5_out, BrLt, comparator_5_eq);
  and and_6 (and_6_out, not_3_out, comparator_6_eq);
  Comparator #(.width(7)) comparator_14 (.a({7{1'b0}}), .b(inst[31:25]), .eq(comparator_14_eq));  // open: gt, lt
  Comparator #(.width(3)) comparator_15 (.a(3'b000), .b(inst[14:12]), .eq(comparator_15_eq));  // open: gt, lt
  Comparator #(.width(7)) comparator_16 (.a(7'b0000011), .b(inst[6:0]), .eq(comparator_16_eq));  // open: gt, lt
  and and_7 (and_7_out, comparator_7_eq, comparator_8_eq);
  Comparator #(.width(7)) comparator_17 (.a(7'b0010111), .b(inst[6:0]), .eq(comparator_17_eq));  // open: gt, lt
  Comparator #(.width(7)) comparator_18 (.a(7'b1100111), .b(inst[6:0]), .eq(comparator_18_eq));  // open: gt, lt
  Comparator #(.width(3)) comparator_19 (.a(3'b111), .b(inst[14:12]), .eq(comparator_19_eq));  // open: gt, lt
  Comparator #(.width(3)) comparator_20 (.a(3'b100), .b(inst[14:12]), .eq(comparator_20_eq));  // open: gt, lt
  Comparator #(.width(7)) comparator_21 (.a({7{1'b0}}), .b(inst[31:25]), .eq(comparator_21_eq));  // open: gt, lt
  Comparator #(.width(3)) comparator_22 (.a(3'b101), .b(inst[14:12]), .eq(comparator_22_eq));  // open: gt, lt
  Comparator #(.width(7)) comparator_23 (.a(7'b0100000), .b(inst[31:25]), .eq(comparator_23_eq));  // open: gt, lt
  Comparator #(.width(3)) comparator_24 (.a(3'b101), .b(inst[14:12]), .eq(comparator_24_eq));  // open: gt, lt
  or or_1 (or_1_out, I_Type, R_Type);
  Comparator #(.width(7)) comparator_25 (.a({7{1'b0}}), .b(inst[31:25]), .eq(comparator_25_eq));  // open: gt, lt
  Comparator #(.width(3)) comparator_26 (.a(3'b001), .b(inst[14:12]), .eq(comparator_26_eq));  // open: gt, lt
  or or_2 (or_2_out, I_Type, R_Type);
  Comparator #(.width(3)) comparator_27 (.a(3'b010), .b(inst[14:12]), .eq(comparator_27_eq));  // open: gt, lt
  Comparator #(.width(3)) comparator_28 (.a(3'b000), .b(inst[14:12]), .eq(comparator_28_eq));  // open: gt, lt
  Comparator #(.width(3)) comparator_29 (.a(3'b011), .b(inst[14:12]), .eq(comparator_29_eq));  // open: gt, lt
  Comparator #(.width(3)) comparator_30 (.a(3'b000), .b(inst[14:12]), .eq(comparator_30_eq));  // open: gt, lt
  Comparator #(.width(7)) comparator_31 (.a(7'b0110111), .b(inst[6:0]), .eq(bsel_alu));  // open: gt, lt
  and and_8 (and_8_out, comparator_14_eq, comparator_15_eq);
  or or_3 (or_3_out, I_Type, R_Type);
  or or_4 (or_4_out, I_Type, R_Type);
  Comparator #(.width(3)) comparator_32 (.a(3'b110), .b(inst[14:12]), .eq(comparator_32_eq));  // open: gt, lt
  or or_5 (or_5_out, I_Type, R_Type);
  or or_6 (or_6_out, I_Type, R_Type);
  or or_7 (or_7_out, I_Type, R_Type);
  and and_9 (mul_alu, R_Type, comparator_9_eq, comparator_28_eq);
  and and_10 (mulh_alu, R_Type, comparator_10_eq, comparator_11_eq);
  and and_11 (mulhu_alu, R_Type, comparator_12_eq, comparator_29_eq);
  and and_12 (sub_alu, R_Type, comparator_13_eq, comparator_30_eq);
  and and_13 (and_alu, or_3_out, comparator_19_eq);
  and and_14 (or_alu, or_4_out, comparator_32_eq);
  and and_15 (xor_alu, or_5_out, comparator_20_eq);
  and and_16 (srl_alu, or_6_out, comparator_21_eq, comparator_22_eq);
  and and_17 (sra_alu, or_7_out, comparator_23_eq, comparator_24_eq);
  and and_18 (sll_alu, or_1_out, comparator_25_eq, comparator_26_eq);
  and and_19 (slt_alu, or_2_out, comparator_27_eq);
  Comparator #(.width(7)) comparator_33 (.a(7'b1100011), .b(inst[6:0]), .eq(comparator_33_eq));  // open: gt, lt
  or or_8 (or_8_out, and_1_out, and_2_out, and_3_out, and_4_out, and_5_out, and_6_out);
  and and_20 (add_alu, and_8_out, comparator_16_eq, and_7_out, S_Type, SB_Type, comparator_17_eq, UJ_Type, comparator_18_eq);
  and and_21 (and_21_out, comparator_33_eq, or_8_out);
  // Probe on inst
  Comparator #(.width(7)) comparator_34 (.a(7'b1100111), .b(inst[6:0]), .eq(comparator_34_eq));  // open: gt, lt
  Comparator #(.width(7)) comparator_35 (.a(7'b1101111), .b(inst[6:0]), .eq(comparator_35_eq));  // open: gt, lt
  Comparator #(.mode("unsigned"), .width(3)) comparator_36 (
    .a(3'b000), .b(inst[14:12]), .eq(comparator_36_eq));  // open: gt, lt
  or or_9 (PCSel, comparator_34_eq, comparator_35_eq, and_21_out);
  Comparator #(.width(7)) comparator_37 (.a(7'b0000011), .b(inst[6:0]), .eq(comparator_37_eq));  // open: gt, lt
  Comparator #(.width(7)) comparator_38 (.a(7'b0010011), .b(inst[6:0]), .eq(comparator_38_eq));  // open: gt, lt
  Comparator #(.width(7)) comparator_39 (.a(7'b1100111), .b(inst[6:0]), .eq(comparator_39_eq));  // open: gt, lt
  or or_10 (or_10_out, srl_alu, sra_alu);
  or or_11 (or_11_out, sll_alu, slt_alu);
  or or_12 (or_12_out, sub_alu, bsel_alu, mulh_alu);
  or or_13 (or_13_out, and_alu, xor_alu);
  or or_14 (or_14_out, sra_alu, slt_alu);
  or or_15 (or_15_out, mulhu_alu, bsel_alu);
  or or_16 (MemRW, S_Type, comparator_37_eq);
  Comparator #(.width(7)) comparator_40 (.a(7'b1110011), .b(inst[6:0]), .eq(comparator_40_eq));  // open: gt, lt
  Comparator #(.mode("unsigned"), .width(3)) comparator_41 (
    .a(3'b101), .b(inst[14:12]), .eq(comparator_41_eq));  // open: gt, lt
  Comparator #(.mode("unsigned"), .width(7)) comparator_42 (
    .a(7'b1101111), .b(inst[6:0]), .eq(comparator_42_eq));  // open: gt, lt
  and and_22 (and_22_out, comparator_39_eq, comparator_36_eq);
  or or_17 (ALUSel[2], or_10_out, or_11_out, or_12_out);
  or or_18 (ALUSel[0], or_13_out, or_14_out, or_15_out);
  or or_19 (WBSel[0], R_Type, comparator_38_eq, SB_Type, U_Type);
  Comparator #(.mode("unsigned"), .width(7)) comparator_43 (
    .a(7'b0000011), .b(inst[6:0]), .eq(WBSel_mem));  // open: gt, lt
  or or_20 (WBSel[1], comparator_42_eq, and_22_out);
  Comparator #(.width(7)) comparator_44 (.a(7'b1110011), .b(inst[6:0]), .eq(CSRWen));  // open: gt, lt
  and and_23 (CSRSel, comparator_40_eq, comparator_41_eq);
  nor nor_1 (RegWEn, comparator_45_eq, comparator_46_eq);
  Comparator #(.width(7)) comparator_45 (.a(7'b1100011), .b(inst[6:0]), .eq(comparator_45_eq));  // open: gt, lt
  Comparator #(.width(7)) comparator_46 (.a(7'b0100011), .b(inst[6:0]), .eq(comparator_46_eq));  // open: gt, lt
  or or_21 (or_21_out, mul_alu, mulhu_alu);
  or or_22 (or_22_out, or_alu, xor_alu);
  or or_23 (or_23_out, sll_alu, slt_alu);
  or or_24 (or_24_out, mul_alu, mulhu_alu, mulh_alu);
  Comparator #(.width(7)) comparator_47 (.a(7'b0110011), .b(inst[6:0]), .eq(R_Type));  // open: gt, lt
  Comparator #(.width(7)) comparator_48 (.a(7'b0010011), .b(inst[6:0]), .eq(comparator_48_eq));  // open: gt, lt
  Comparator #(.width(7)) comparator_49 (.a(7'b0000011), .b(inst[6:0]), .eq(comparator_49_eq));  // open: gt, lt
  Comparator #(.width(7)) comparator_50 (.a(7'b1110011), .b(inst[6:0]), .eq(comparator_50_eq));  // open: gt, lt
  Comparator #(.width(7)) comparator_51 (.a(7'b1100111), .b(inst[6:0]), .eq(comparator_51_eq));  // open: gt, lt
  Comparator #(.width(7)) comparator_52 (.a(7'b0100011), .b(inst[6:0]), .eq(S_Type));  // open: gt, lt
  Comparator #(.width(7)) comparator_53 (.a(7'b1100011), .b(inst[6:0]), .eq(SB_Type));  // open: gt, lt
  Comparator #(.width(7)) comparator_54 (.a(7'b0010111), .b(inst[6:0]), .eq(comparator_54_eq));  // open: gt, lt
  Comparator #(.width(7)) comparator_55 (.a(7'b0110111), .b(inst[6:0]), .eq(comparator_55_eq));  // open: gt, lt
  Comparator #(.width(7)) comparator_56 (.a(7'b1101111), .b(inst[6:0]), .eq(UJ_Type));  // open: gt, lt
  or or_25 (or_25_out, sub_alu, bsel_alu, mulh_alu);
  or or_26 (ALUSel[3], or_21_out, or_25_out);
  or or_27 (ALUSel[1], or_22_out, or_23_out, or_24_out);
  or or_28 (U_Type, comparator_54_eq, comparator_55_eq);
  or or_29 (I_Type, comparator_48_eq, comparator_49_eq, comparator_50_eq, comparator_51_eq);
  not not_4 (not_4_out, S_Type);
  not not_5 (not_5_out, SB_Type);
  and and_24 (and_24_out, I_Type, SB_Type);
  nor nor_2 (ASel, R_Type, I_Type, S_Type, SB_Type);
  nor nor_3 (BSel, R_Type, S_Type, SB_Type);
  nor nor_4 (nor_4_out, R_Type, I_Type, U_Type, UJ_Type);
  and and_25 (and_25_out, S_Type, not_5_out);
  and and_26 (and_26_out, not_4_out, SB_Type);
  nor nor_5 (ImmSel[0], R_Type, S_Type, U_Type, UJ_Type, and_24_out);
  and and_27 (ImmSel[1], nor_4_out, and_25_out, and_26_out);
  nor nor_6 (ImmSel[2], R_Type, I_Type, S_Type, SB_Type, UJ_Type);
  // Probe on ImmSel

  assign BrUn = inst[13];

  // Other names for the same wires on the sheet: ALUSel_0 = ALUSel[0]; ALUSel_1 = ALUSel[1]; ALUSel_2 = ALUSel[2];
  //   ALUSel_3 = ALUSel[3]; opcode[6:0] = inst[6:0]; funct3[2:0] = inst[14:12]; funct7[6:0] = inst[31:25];
  //   WBSel_alu = WBSel[0]; WBSel_pc = WBSel[1]

  // Notes on the sheet:
  //   INPUTS to your circuit
  //   Branch Comp
  //   DON'T CHANGE THE LOCATIONS OF THE INPUTS AND OUTPUTS!
  //   OUTPUT from your circuit
  //   ImmSel_0
  //   ImmSel_2
  //   ImmSel_1
endmodule
