// Logisim project cpu.circ as structural Verilog: 1 circuit, main circuit cpu
// ASel
module cpu (
  input  clk,
  input  [31:0] INSTRUCTION,
  input  [31:0] READ_DATA,
  output [31:0] WRITE_ADDRESS,
  output [31:0] PROGRAM_COUNTER,
  output [31:0] ra,
  output [31:0] sp,
  output [31:0] t0,
  output [31:0] t1,
  output [31:0] t2,
  output [31:0] s0,
  output [31:0] s1,
  output [31:0] a0,
  output [31:0] tohost,
  output [3:0] WRITE_ENABLE,
  output [31:0] WRITE_DATA
);

  wire ASel, BrEq, BrLt, Brun, BSel, CSRSel, CSRWen, MemRW, PCSel, RegWEn;
  wire [1:0] WBSel;
  wire [2:0] funct3, Immsel;
  wire [3:0] ALUSel, multiplexer_5_out;
  wire [4:0] AddrA, AddrB, AddrD;
  wire [31:0] adder_1_out, adder_2_out, ALUInA, ALUInB, bit_extender_1_out, bit_extender_2_out,
       bit_extender_3_out, CSR_din, imm, INSTRUCTION_choose, INSTRUCTION_STATE, multiplexer_1_out,
       multiplexer_8_out, PROGRAM_COUNTER_STATE, rs1, WB;

  Adder #(.width(32)) adder_1 (.a(PROGRAM_COUNTER), .b(32'h4), .out(adder_1_out));  // open: cin, cout
  Multiplexer #(.enable("false"), .width(32)) multiplexer_1 (
    .in0(adder_1_out), .in1(WRITE_ADDRESS), .out(multiplexer_1_out), .sel(PCSel));
  Register #(.width(32)) PC (.D(multiplexer_1_out), .clk(clk), .Q(PROGRAM_COUNTER));  // open: en, clr
  // Probe on PROGRAM_COUNTER
  // Probe on PROGRAM_COUNTER
  Register #(.width(32)) pcD (.D(PROGRAM_COUNTER), .clk(clk), .Q(PROGRAM_COUNTER_STATE));  // open: en, clr
  // Probe on Immsel
  // Probe on PROGRAM_COUNTER_STATE
  // Probe on {INSTRUCTION_STATE[31:25], AddrB, AddrA, funct3, AddrD, INSTRUCTION_STATE[6:0]}
  // Probe on AddrD
  // Probe on imm
  imm_gen imm_gen_1 (
    .inst({INSTRUCTION_STATE[31:25], AddrB, AddrA, funct3, AddrD, INSTRUCTION_STATE[6:0]}), .ImmSel(Immsel),
    .imm(imm));
  // Probe on INSTRUCTION_choose
  Multiplexer #(.enable("false"), .width(32)) multiplexer_2 (
    .in0(INSTRUCTION), .in1(32'h13), .out(INSTRUCTION_choose), .sel(PCSel));
  // Probe on AddrD
  // Probe on INSTRUCTION_choose
  // Probe on WB
  Register #(.width(32)) irstD (
    .D(INSTRUCTION_choose), .clk(clk),
    .Q({INSTRUCTION_STATE[31:25], AddrB, AddrA, funct3, AddrD, INSTRUCTION_STATE[6:0]}));  // open: en, clr
  // Probe on {INSTRUCTION_STATE[31:25], AddrB, AddrA, funct3, AddrD, INSTRUCTION_STATE[6:0]}
  // Probe on {INSTRUCTION_STATE[31:25], AddrB, AddrA, funct3, AddrD, INSTRUCTION_STATE[6:0]}
  control_logic control_logic_1 (
    .CSRWen(CSRWen), .PCSel(PCSel), .RegWEn(RegWEn), .ImmSel(Immsel), .BrUn(Brun), .ASel(ASel), .BSel(BSel),
    .ALUSel(ALUSel), .MemRW(MemRW), .WBSel(WBSel), .CSRSel(CSRSel),
    .inst({INSTRUCTION_STATE[31:25], AddrB, AddrA, funct3, AddrD, INSTRUCTION_STATE[6:0]}), .BrEq(BrEq),
    .BrLt(BrLt));
  regfile regfile_1 (
    .rs1(AddrA), .rs2(AddrB), .rd(AddrD), .Write_Data(WB), .RegWEn(RegWEn), .clk(clk), .ra(ra), .sp(sp),
    .t0(t0), .t1(t1), .t2(t2), .s0(s0), .s1(s1), .a0(a0), .Read_Data_1(rs1), .Read_Data_2(WRITE_DATA));
  // Probe on ALUSel
  // Probe on WBSel
  // Probe on BSel
  // Probe on imm
  Multiplexer #(.enable("false"), .width(32)) multiplexer_3 (.in0(WRITE_DATA), .in1(imm), .out(ALUInB), .sel(BSel));
  Multiplexer #(.enable("false"), .width(32)) multiplexer_4 (
    .in0(rs1), .in1(PROGRAM_COUNTER_STATE), .out(ALUInA), .sel(ASel));
  // Probe on PROGRAM_COUNTER_STATE
  // Probe on ASel
  branch_comp branch_comp_1 (.rs1(rs1), .rs2(WRITE_DATA), .BrUn(Brun), .BrEq(BrEq), .BrLt(BrLt));
  // Probe on ALUInB
  // Probe on ALUInA
  // Probe on ALUSel
  alu alu_1 (.Result(WRITE_ADDRESS), .A(ALUInA), .B(ALUInB), .ALUSel(ALUSel));
  // Probe on WRITE_ADDRESS
  Multiplexer #(.enable("false"), .select(3), .width(4)) multiplexer_5 (
    .in0(4'b0001), .in1(4'b0011), .in2(4'b1111), .out(multiplexer_5_out), .sel(funct3));  // open: in3, in4, in5, in6, in7
  // Probe on WRITE_ENABLE
  Multiplexer #(.enable("false"), .width(4)) multiplexer_6 (
    .in0(4'b0000), .in1(multiplexer_5_out), .out(WRITE_ENABLE), .sel(MemRW));
  assign bit_extender_1_out = {{27{1'b0}}, AddrA};  // Bit_Extender bit_extender_1
  Multiplexer #(.enable("false"), .width(32)) multiplexer_7 (
    .in0(rs1), .in1(bit_extender_1_out), .out(CSR_din), .sel(CSRSel));
  // Probe on CSR_din
  // Probe on READ_DATA
  assign bit_extender_2_out = {{24{READ_DATA[7]}}, READ_DATA[7:0]};  // Bit_Extender bit_extender_2
  assign bit_extender_3_out = {{16{READ_DATA[15]}}, READ_DATA[15:0]};  // Bit_Extender bit_extender_3
  // Probe on PROGRAM_COUNTER_STATE
  Adder #(.width(32)) adder_2 (.a(PROGRAM_COUNTER_STATE), .b(32'h4), .out(adder_2_out));  // open: cin, cout
  Multiplexer #(.enable("false"), .select(3), .width(32)) multiplexer_8 (
    .in0(bit_extender_2_out), .in1(bit_extender_3_out), .in2(READ_DATA), .out(multiplexer_8_out), .sel(funct3));  // open: in3, in4, in5, in6, in7
  // Probe on adder_2_out
  // Probe on WRITE_ADDRESS
  // Probe on WBSel
  csr csr_1 (.CSR_address(12'h51e), .CSR_din(CSR_din), .CSR_WE(CSRWen), .clk(clk), .tohost(tohost));
  // Probe on WB
  Multiplexer #(.enable("false"), .select(2), .width(32)) multiplexer_9 (
    .in0(multiplexer_8_out), .in1(WRITE_ADDRESS), .in2(adder_2_out), .out(WB), .sel(WBSel));  // open: in3

  // Other names for the same wires on the sheet: ALUOutput[31:0] = WRITE_ADDRESS;
  //   INSTRUCTION_STATE[24:7] = {AddrB, AddrA, funct3, AddrD}; rs2[31:0] = WRITE_DATA

  // Notes on the sheet:
  //   Output to IMEM
  //   IF
  //   IMEM (do **NOT** move this)
  //   Inputs from IMEM
  //   decode
  //   for like  bne that need to save next pc of current pc
  //   Inputs/Outputs for testing. Do **NOT** move these.
  //   NOP
  //   kill instruction for jal or bne  of having data hazard
  //   for deviding two stage pipeline
  //   Control logic
  //   Outputs To DMEM
  //   Execute
  //   DMEM (do **NOT** move this)
  //   Inputs From DMEM
  //   NOTE
  //   This is two stage pipeline CPU, and it has such operating process, that  one fetch the instruction and the two begins to execute and remember the three it finish like "write"  operation for memory and regfile
endmodule
