// Logisim project imm_gen.circ as structural Verilog: 1 circuit, main circuit imm_gen
module imm_gen (
  input  [31:0] inst,
  input  [2:0] ImmSel,
  output [31:0] imm
);

  wire [31:11] imm_I, imm_S;
  wire [31:12] imm_SB;
  wire [31:20] imm_UJ;

  assign imm_I = {{20{inst[31]}}, inst[31]};  // Bit_Extender bit_extender_1
  assign imm_S = {{20{inst[31]}}, inst[31]};  // Bit_Extender bit_extender_2
  // Probe on inst[11:8]
  assign imm_SB = {{19{inst[31]}}, inst[31]};  // Bit_Extender bit_extender_3
  assign imm_UJ = {{11{inst[31]}}, inst[31]};  // Bit_Extender bit_extender_4
  // Probe on {imm_I, inst[30:20]}
  // Probe on {imm_S, inst[30:25], inst[11:7]}
  // Probe on {imm_SB, inst[7], inst[30:25], inst[11:8], 1'b0}
  // Probe on ImmSel
  // Probe on imm
  Multiplexer #(.enable("false"), .select(3), .width(32)) multiplexer_1 (
    .in0({32{1'b0}}), .in1({imm_I, inst[30:20]}), .in2({imm_S, inst[30:25], inst[11:7]}),
    .in3({imm_SB, inst[7], inst[30:25], inst[11:8], 1'b0}), .in4({inst[31:12], {12{1'b0}}}),
    .in5({imm_UJ, inst[19:12], inst[20], inst[30:21], 1'b0}), .out(imm), .sel(ImmSel));  // open: in6, in7

  // Other names for the same wires on the sheet: imm_S[10:0] = {inst[30:25], inst[11:7]};
  //   imm_SB[11:1] = {inst[7], inst[30:25], inst[11:8]}; imm_U[31:12] = inst[31:12]; imm_I[10:0] = inst[30:20];
  //   imm_UJ[19:1] = {inst[19:12], inst[20], inst[30:21]}

  // Notes on the sheet:
  //   INPUTS to your circuit
  //   DON'T CHANGE THE LOCATIONS OF THE INPUTS AND OUTPUTS!
  //   OUTPUT from your circuit
endmodule
