// Logisim project regfile.circ as structural Verilog: 1 circuit, main circuit regfile
module regfile (
  input  [4:0] rs1,
  input  [4:0] rs2,
  input  [4:0] rd,
  input  [31:0] Write_Data,
  input  RegWEn,
  input  clk,
  output [31:0] ra,
  output [31:0] sp,
  output [31:0] t0,
  output [31:0] t1,
  output [31:0] t2,
  output [31:0] s0,
  output [31:0] s1,
  output [31:0] a0,
  output [31:0] Read_Data_1,
  output [31:0] Read_Data_2
);

  wire write_en_0, write_en_1, write_en_2, write_en_3, write_en_4, write_en_5, write_en_6, write_en_7,
       write_en_8, write_en_9, write_en_10, write_en_11, write_en_12, write_en_13, write_en_14, write_en_15,
       write_en_16, write_en_17, write_en_18, write_en_19, write_en_20, write_en_21, write_en_22,
       write_en_23, write_en_24, write_en_25, write_en_26, write_en_27, write_en_28, write_en_29,
       write_en_30, write_en_31;
  wire [31:0] a1, a2, a3, a4, a5, a6, a7, gp, s2, s3, s4, s5, s6, s7, s8, s9, s10, s11, t3, t4, t5, t6, tp;

  Demultiplexer #(.enable("false"), .select(5)) demultiplexer_1 (
    .out0(write_en_0), .out1(write_en_1), .out2(write_en_2), .out3(write_en_3), .out4(write_en_4),
    .out5(write_en_5), .out6(write_en_6), .out7(write_en_7), .out8(write_en_8), .out9(write_en_9),
    .out10(write_en_10), .out11(write_en_11), .out12(write_en_12), .out13(write_en_13), .out14(write_en_14),
    .out15(write_en_15), .out16(write_en_16), .out17(write_en_17), .out18(write_en_18), .out19(write_en_19),
    .out20(write_en_20), .out21(write_en_21), .out22(write_en_22), .out23(write_en_23), .out24(write_en_24),
    .out25(write_en_25), .out26(write_en_26), .out27(write_en_27), .out28(write_en_28), .out29(write_en_29),
    .out30(write_en_30), .out31(write_en_31), .in(RegWEn), .sel(rd));
  Multiplexer #(.enable("false"), .select(5), .width(32)) multiplexer_1 (
    .in0({32{1'b0}}), .in1(ra), .in2(sp), .in3(gp), .in4(tp), .in5(t0), .in6(t1), .in7(t2), .in8(s0),
    .in9(s1), .in10(a0), .in11(a1), .in12(a2), .in13(a3), .in14(a4), .in15(a5), .in16(a6), .in17(a7),
    .in18(s2), .in19(s3), .in20(s4), .in21(s5), .in22(s6), .in23(s7), .in24(s8), .in25(s9), .in26(s10),
    .in27(s11), .in28(t3), .in29(t4), .in30(t5), .in31(t6), .out(Read_Data_1), .sel(rs1));
  Register #(.width(32)) register_1 (.D(Write_Data), .en(write_en_8), .clk(clk), .Q(s0));  // open: clr
  Register #(.width(32)) register_2 (.D(Write_Data), .en(write_en_1), .clk(clk), .Q(ra));  // open: clr
  Register #(.width(32)) register_3 (.D(Write_Data), .en(write_en_2), .clk(clk), .Q(sp));  // open: clr
  Register #(.width(32)) register_4 (.D(Write_Data), .en(write_en_3), .clk(clk), .Q(gp));  // open: clr
  Register #(.width(32)) register_5 (.D(Write_Data), .en(write_en_4), .clk(clk), .Q(tp));  // open: clr
  Register #(.width(32)) register_6 (.D(Write_Data), .en(write_en_5), .clk(clk), .Q(t0));  // open: clr
  Register #(.width(32)) register_7 (.D(Write_Data), .en(write_en_6), .clk(clk), .Q(t1));  // open: clr
  Register #(.width(32)) register_8 (.D(Write_Data), .en(write_en_7), .clk(clk), .Q(t2));  // open: clr
  Register #(.width(32)) register_9 (.D(Write_Data), .en(write_en_9), .clk(clk), .Q(s1));  // open: clr
  Register #(.width(32)) register_10 (.D(Write_Data), .en(write_en_10), .clk(clk), .Q(a0));  // open: clr
  Register #(.width(32)) register_11 (.D(Write_Data), .en(write_en_11), .clk(clk), .Q(a1));  // open: clr
  Register #(.width(32)) register_12 (.D(Write_Data), .en(write_en_12), .clk(clk), .Q(a2));  // open: clr
  Register #(.width(32)) register_13 (.D(Write_Data), .en(write_en_13), .clk(clk), .Q(a3));  // open: clr
  Register #(.width(32)) register_14 (.D(Write_Data), .en(write_en_14), .clk(clk), .Q(a4));  // open: clr
  Register #(.width(32)) register_15 (.D(Write_Data), .en(write_en_15), .clk(clk), .Q(a5));  // open: clr
  Register #(.width(32)) register_16 (.D(Write_Data), .en(write_en_16), .clk(clk), .Q(a6));  // open: clr
  Multiplexer #(.enable("false"), .select(5), .width(32)) multiplexer_2 (
    .in0({32{1'b0}}), .in1(ra), .in2(sp), .in3(gp), .in4(tp), .in5(t0), .in6(t1), .in7(t2), .in8(s0),
    .in9(s1), .in10(a0), .in11(a1), .in12(a2), .in13(a3), .in14(a4), .in15(a5), .in16(a6), .in17(a7),
    .in18(s2), .in19(s3), .in20(s4), .in21(s5), .in22(s6), .in23(s7), .in24(s8), .in25(s9), .in26(s10),
    .in27(s11), .in28(t3), .in29(t4), .in30(t5), .in31(t6), .out(Read_Data_2), .sel(rs2));
  Register #(.width(32)) register_17 (.D(Write_Data), .en(write_en_17), .clk(clk), .Q(a7));  // open: clr
  Register #(.width(32)) register_18 (.D(Write_Data), .en(write_en_18), .clk(clk), .Q(s2));  // open: clr
  Register #(.width(32)) register_19 (.D(Write_Data), .en(write_en_19), .clk(clk), .Q(s3));  // open: clr
  Register #(.width(32)) register_20 (.D(Write_Data), .en(write_en_20), .clk(clk), .Q(s4));  // open: clr
  Register #(.width(32)) register_21 (.D(Write_Data), .en(write_en_21), .clk(clk), .Q(s5));  // open: clr
  Register #(.width(32)) register_22 (.D(Write_Data), .en(write_en_22), .clk(clk), .Q(s6));  // open: clr
  Register #(.width(32)) register_23 (.D(Write_Data), .en(write_en_23), .clk(clk), .Q(s7));  // open: clr
  Register #(.width(32)) register_24 (.D(Write_Data), .en(write_en_24), .clk(clk), .Q(s8));  // open: clr
  Register #(.width(32)) register_25 (.D(Write_Data), .en(write_en_25), .clk(clk), .Q(s9));  // open: clr
  Register #(.width(32)) register_26 (.D(Write_Data), .en(write_en_26), .clk(clk), .Q(s10));  // open: clr
  Register #(.width(32)) register_27 (.D(Write_Data), .en(write_en_27), .clk(clk), .Q(s11));  // open: clr
  Register #(.width(32)) register_28 (.D(Write_Data), .en(write_en_28), .clk(clk), .Q(t3));  // open: clr
  Register #(.width(32)) register_29 (.D(Write_Data), .en(write_en_29), .clk(clk), .Q(t4));  // open: clr
  Register #(.width(32)) register_30 (.D(Write_Data), .en(write_en_30), .clk(clk), .Q(t5));  // open: clr
  Register #(.width(32)) register_31 (.D(Write_Data), .en(write_en_31), .clk(clk), .Q(t6));  // open: clr

  // Other names for the same wires on the sheet: read_data1[31:0] = Read_Data_1; read_data2[31:0] = Read_Data_2;
  //   read_reg1[4:0] = rs1; read_reg2[4:0] = rs2; write_en = RegWEn; write_reg[4:0] = rd; x8[31:0] = s0

  // Notes on the sheet:
  //   INPUTS to your circuit
  //   DON'T CHANGE THE LOCATIONS OF THE INPUTS AND OUTPUTS!
  //   These are DEBUG/TEST outputs from your circuit.
  //   OUTPUTS from your circuit
endmodule
